# Fritzing sketch Tank1SCHEMS_finalDRAFT3_USBCable_Fritzing (saved by Fritzing 0.9.2b)
circuit board: 9.79026cm x 6.37514cm
breadboards: 1

parts:
  Part1 = Arduino Uno (Rev3)
  R7 = Resistor [tolerance=±5% resistance=220 package=THT]
  LED3 = LED - 5mm [color="Yellow (595nm)" package="5 mm [THT]"]
  M2 = DC Motor
  M1 = DC Motor
  VCC1 = 4 x AAA Battery Mount
  U3 = HC-SR04 [chip_label=IC package="SIP (Single Inline) [THT]"]
  Part5 = Pololu Motor Driver 1A Dual TB6612FNG

nets:
  N1: Part1.D8, Part5.BIN2
  N2: Part1.D9_PWM, Part5.PWMB
  GND: Part1.GND, LED3.cathode, VCC1.-, U3.GND, Part5.GND
  N3: Part1.D2, U3.Trig, U3.Echo
  N4: Part1.D3_PWM, Part5.PWMA
  N5: Part1.D4, Part5.AIN2
  N6: Part1.D5_PWM, Part5.AIN1
  N7: Part1.D6_PWM, R7.Pin_1, Part5.STBY
  N8: Part1.D7, Part5.BIN1
  VCC: Part1.5V, U3.Vcc, Part5.VCC
  N9: R7.Pin_0, LED3.anode
  N10: M2.pin_1, Part5.B02
  N11: M2.pin_2, Part5.B01
  N12: M1.pin_1, Part5.A01
  N13: M1.pin_2, Part5.A02
  N14: VCC1.+, Part5.VM

custom parts:
  HC-SR04: HC-SR04 ultrasound distance sensor
  Pololu Motor Driver 1A Dual TB6612FNG: The TB6612FNG motor driver can control up to two DC motors at a constant current of 1.2A (3.2A peak). Two input signals (IN1 and IN2) can be used to control the motor in one of four function modes - CW, CCW, short-brake, and stop. The two motor outputs (A and B) can be separately controlled, the speed of each motor is controlled via a PWM input signal with a frequency up to 100kHz. The STBY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
